# Fritzing sketch MPU6050_esp32 (saved by Fritzing 0.9.2b)
breadboards: 1

parts:
  J1 = Hornbill ESP 32 [package=THT]
  OLED_I2C1 = OLED 128x64 I2C Monochrome Display
  GY1 = MPU-6050 Board GY-521 [form="♀ (female)" package=THT]

nets:
  N1: J1.pin_13, OLED_I2C1.SCK, GY1.pin3
  N2: J1.pin_16, OLED_I2C1.SDA, GY1.pin4
  N3: J1.pin_18, OLED_I2C1.GND, GY1.pin2
  N4: J1.pin_19, OLED_I2C1.VDD
  N5: J1.pin_37, GY1.pin1

custom parts:
  Hornbill ESP 32: A generic force sensitive resistor
  MPU-6050 Board GY-521: Acelerometro y Giroscopio MPU-6050 Board GY-521
