# Fritzing sketch Blink_esp32 (saved by Fritzing 0.9.2b)
breadboards: 1

parts:
  J1 = Hornbill ESP 32 [package=THT]
  LED1 = LED - 5mm [color="Red (633nm)" package="5 mm [THT]"]
  R1 = Resistor [tolerance=±5% resistance=220 package=THT]

nets:
  N1: J1.pin_27, R1.Pin_0
  N2: J1.pin_32, LED1.cathode
  N3: LED1.anode, R1.Pin_1

custom parts:
  Hornbill ESP 32: A generic force sensitive resistor
