# Fritzing sketch RGB_esp32 (saved by Fritzing 0.9.2b)
breadboards: 1

parts:
  J1 = Hornbill ESP 32 [package=THT]
  R1 = Resistor [tolerance=±5% resistance=220 package=THT]
  LED1 = RGB LED (com. cathode, rgb) [package="5 mm [THT]"]
  R3 = Resistor [tolerance=±5% resistance=220 package=THT]
  R2 = Resistor [tolerance=±5% resistance=220 package=THT]

nets:
  N1: J1.pin_19, LED1.green_anode
  N2: J1.pin_27, R2.Pin_0
  N3: J1.pin_28, R1.Pin_0
  N4: J1.pin_29, R3.Pin_0
  N5: R1.Pin_1, LED1.common_cathode
  N6: LED1.red_anode, R3.Pin_1
  N7: LED1.blue_anode, R2.Pin_1

custom parts:
  Hornbill ESP 32: A generic force sensitive resistor
