# Fritzing sketch Ultrasonic_esp32 (saved by Fritzing 0.9.2b)
breadboards: 1

parts:
  J1 = Hornbill ESP 32 [package=THT]
  Part1 = SRF05 Ultrasonic Rangefinder
  OLED_I2C1 = OLED 128x64 I2C Monochrome Display

nets:
  N1: J1.pin_10, Part1.Trig
  N2: J1.pin_11, Part1.Echo
  N3: J1.pin_13, OLED_I2C1.SCK
  N4: J1.pin_16, OLED_I2C1.SDA
  GND: J1.pin_18, Part1.GND, OLED_I2C1.GND
  N5: J1.pin_19, OLED_I2C1.VDD
  N6: J1.pin_37, Part1.VCC

custom parts:
  Hornbill ESP 32: A generic force sensitive resistor
