# Fritzing sketch DHT11 with ESP32 (saved by Fritzing 0.9.2b)
breadboards: 1

parts:
  J1 = Hornbill ESP 32 [package=THT]
  Part2 = KY-015 Temperature & Humidity Sensor Module [package="Breakout board"]

nets:
  N1: J1.pin_6, Part2.Vin
  N2: J1.pin_18, Part2.G
  N3: J1.pin_19, Part2.+

custom parts:
  Hornbill ESP 32: A generic force sensitive resistor
  KY-015 Temperature & Humidity Sensor Module: KY-015 temperature and humidity sensor module, provides a low-latency serial interface to measure humidity and temperature.
